// Logisim project EP01.circ as structural Verilog: 5 circuits, main circuit main
module main (
);

  soma_4bit soma_4bit_1 ();  // open: B3, A3, B2, A2, B1, A1, B0, A0, C0, S3, S2, S1, S0, Ci0
endmodule

module meia_soma (
  input  X,
  input  Y,
  output S1,
  output out_4
);

  and and_1 (out_4, Y, X);
  xor xor_1 (S1, X, Y);
endmodule

module soma_completa (
  input  A0,
  input  B0,
  input  Ci0,
  output S0,
  output Co0
);

  wire meia_soma_1_out_4, meia_soma_1_s1, meia_soma_2_out_4;

  meia_soma meia_soma_1 (.X(A0), .Y(B0), .S1(meia_soma_1_s1), .out_4(meia_soma_1_out_4));
  meia_soma meia_soma_2 (.X(meia_soma_1_s1), .Y(Ci0), .S1(S0), .out_4(meia_soma_2_out_4));
  or or_1 (Co0, meia_soma_1_out_4, meia_soma_2_out_4);
endmodule

module soma_4bit (
  input  A3,
  input  A2,
  input  A1,
  input  A0,
  input  B3,
  input  B2,
  input  B1,
  input  B0,
  input  Ci0,
  output S3,
  output S2,
  output S1,
  output S0,
  output C0
);

  wire soma_completa_2_co0, soma_completa_3_co0, soma_completa_4_co0;

  soma_completa soma_completa_1 (.A0(A3), .B0(B3), .Ci0(soma_completa_2_co0), .S0(S3), .Co0(C0));
  soma_completa soma_completa_2 (.A0(A2), .B0(B2), .Ci0(soma_completa_3_co0), .S0(S2), .Co0(soma_completa_2_co0));
  soma_completa soma_completa_3 (.A0(A1), .B0(B1), .Ci0(soma_completa_4_co0), .S0(S1), .Co0(soma_completa_3_co0));
  soma_completa soma_completa_4 (.A0(A0), .B0(B0), .Ci0(Ci0), .S0(S0), .Co0(soma_completa_4_co0));
endmodule

module decodificador (
);

  wire soma_completa_2_co0, soma_completa_4_co0;

  soma_4bit soma_4bit_1 ();  // open: B3, A3, B2, A2, B1, A1, B0, A0, C0, S3, S2, S1, S0, Ci0
  soma_completa soma_completa_1 (.Ci0(soma_completa_2_co0));  // open: A0, B0, S0, Co0
  soma_completa soma_completa_2 (.Co0(soma_completa_2_co0));  // open: A0, B0, Ci0, S0
  soma_completa soma_completa_3 (.Ci0(soma_completa_4_co0));  // open: A0, B0, S0, Co0
  soma_completa soma_completa_4 (.Co0(soma_completa_4_co0));  // open: A0, B0, Ci0, S0
endmodule
