// Logisim project EP02.circ as structural Verilog: 5 circuits, main circuit MUX
module MUX (
  input  M,
  input  N,
  input  O,
  input  P,
  input  Op1,
  input  Op0,
  output S
);

  wire and_1_out, and_2_out, and_3_out, and_4_out, not_1_out, not_2_out, not_3_out, not_4_out;

  not not_1 (not_1_out, Op1);
  not not_2 (not_2_out, Op0);
  not not_3 (not_3_out, Op1);
  not not_4 (not_4_out, Op0);
  and and_1 (and_1_out, M, not_1_out, not_2_out);
  and and_2 (and_2_out, N, not_3_out, Op0);
  and and_3 (and_3_out, O, Op1, not_4_out);
  and and_4 (and_4_out, P, Op1, Op0);
  or or_1 (S, and_1_out, and_2_out, and_3_out, and_4_out);
endmodule

module MAIN (
);

  MUX mux_1 ();  // open: M, N, O, P, S, Op1, Op0
endmodule

module SOMA (
  input  A,
  input  B,
  input  Cin,
  output S,
  output Cout
);

  wire and_1_out, and_2_out, xor_1_out;

  xor xor_1 (xor_1_out, A, B);
  and and_1 (and_1_out, A, B);
  xor xor_2 (S, xor_1_out, Cin);
  and and_2 (and_2_out, xor_1_out, Cin);
  or or_1 (Cout, and_2_out, and_1_out);
endmodule

module ULA_1bit (
  input  Bivent,
  input  A,
  input  Cin,
  input  B,
  input  Op1,
  input  Op0,
  output S,
  output Cout
);

  wire and_1_out, mux_pequeno_1_s, not_1_out, not_2_out, or_1_out, soma_1_s;

  not not_1 (not_1_out, B);
  MUX_pequeno mux_pequeno_1 (.B(B), .S(mux_pequeno_1_s), .Bivent(Bivent), .nB(not_1_out));
  and and_1 (and_1_out, A, B);
  or or_1 (or_1_out, A, B);
  not not_2 (not_2_out, A);
  SOMA soma_1 (.A(A), .B(mux_pequeno_1_s), .Cin(Cin), .S(soma_1_s), .Cout(Cout));
  MUX mux_1 (.M(and_1_out), .N(or_1_out), .O(not_2_out), .P(soma_1_s), .S(S), .Op1(Op1), .Op0(Op0));
endmodule

module MUX_pequeno (
  input  Bivent,
  input  B,
  input  nB,
  output S
);

  wire and_1_out, and_2_out, not_1_out, not_2_out;

  not not_1 (not_1_out, nB);
  and and_1 (and_1_out, B, not_1_out, Bivent);
  not not_2 (not_2_out, B);
  and and_2 (and_2_out, not_2_out, nB, Bivent);
  or or_1 (S, and_1_out, and_2_out);
endmodule
